// Logisim project Es 4.circ as structural Verilog: 4 circuits, main circuit 4.1
module _4_1 (
  output A0,
  output A1,
  output A2,
  output A3
);

  wire clock_1_out, n3_2_1_1_carry_2, n3_2_1_1_sum, n3_2_1_2_carry_2, n3_2_1_2_sum, n3_2_1_3_carry_2,
       n3_2_1_3_sum, n3_2_1_4_sum;

  _3_2_1 u_3_2_1_1 (.Carry(1'b0), .A(1'b1), .B(A0), .Sum(n3_2_1_1_sum), .Carry_2(n3_2_1_1_carry_2));
  _3_2_1 u_3_2_1_2 (.Carry(n3_2_1_1_carry_2), .A(1'b0), .B(A1), .Sum(n3_2_1_2_sum), .Carry_2(n3_2_1_2_carry_2));
  _3_2_1 u_3_2_1_3 (.Carry(n3_2_1_2_carry_2), .A(1'b0), .B(A2), .Sum(n3_2_1_3_sum), .Carry_2(n3_2_1_3_carry_2));
  _3_2_1 u_3_2_1_4 (.Carry(n3_2_1_3_carry_2), .A(A3), .B(1'b0), .Sum(n3_2_1_4_sum));  // open: Carry_2
  Clock clock_1 (.out(clock_1_out));
  D_Flip_Flop d_ff_1 (.clk(clock_1_out), .D(n3_2_1_1_sum), .Q(A0));  // open: Qn, preset, en, reset
  D_Flip_Flop d_ff_2 (.clk(clock_1_out), .D(n3_2_1_2_sum), .Q(A1));  // open: Qn, preset, en, reset
  D_Flip_Flop d_ff_3 (.clk(clock_1_out), .D(n3_2_1_3_sum), .Q(A2));  // open: Qn, preset, en, reset
  D_Flip_Flop d_ff_4 (.clk(clock_1_out), .D(n3_2_1_4_sum), .Q(A3));  // open: Qn, preset, en, reset
endmodule

module _4_2_1 (
  input  S,
  output A0,
  output A1,
  output A2,
  output A3
);

  wire clock_1_out, multiplexer_1_out, n3_2_1_1_carry_2, n3_2_1_1_sum, n3_2_1_2_carry_2, n3_2_1_2_sum,
       n3_2_1_3_carry_2, n3_2_1_3_sum, n3_2_1_4_sum, not_1_out, undriven;

  Clock clock_1 (.out(clock_1_out));
  Multiplexer #(.enable("false")) multiplexer_1 (
    .in0(1'b1), .in1(clock_1_out), .out(multiplexer_1_out), .sel(not_1_out));
  not not_1 (not_1_out, S);
  _3_2_1 u_3_2_1_1 (.Carry(1'b0), .A(1'b1), .B(A0), .Sum(n3_2_1_1_sum), .Carry_2(n3_2_1_1_carry_2));
  _3_2_1 u_3_2_1_2 (.Carry(n3_2_1_1_carry_2), .A(1'b0), .B(A1), .Sum(n3_2_1_2_sum), .Carry_2(n3_2_1_2_carry_2));
  _3_2_1 u_3_2_1_3 (.Carry(n3_2_1_2_carry_2), .A(1'b0), .B(A2), .Sum(n3_2_1_3_sum), .Carry_2(n3_2_1_3_carry_2));
  _3_2_1 u_3_2_1_4 (.Carry(n3_2_1_3_carry_2), .A(A3), .B(1'b0), .Sum(n3_2_1_4_sum));  // open: Carry_2
  D_Flip_Flop d_ff_1 (
    .clk(multiplexer_1_out), .D(n3_2_1_1_sum), .Q(A0), .preset(undriven), .en(undriven));  // open: Qn, reset
  D_Flip_Flop d_ff_2 (.clk(multiplexer_1_out), .D(n3_2_1_2_sum), .Q(A1));  // open: Qn, preset, en, reset
  D_Flip_Flop d_ff_3 (.clk(multiplexer_1_out), .D(n3_2_1_3_sum), .Q(A2));  // open: Qn, preset, en, reset
  D_Flip_Flop d_ff_4 (.clk(multiplexer_1_out), .D(n3_2_1_4_sum), .Q(A3));  // open: Qn, preset, en, reset
endmodule

module _4_2_2 (
  input  S,
  input  R,
  output A0,
  output A1,
  output A2,
  output A3
);

  wire and_1_out, and_2_out, and_3_out, and_4_out, clock_1_out, multiplexer_1_out, n3_2_1_1_carry_2,
       n3_2_1_1_sum, n3_2_1_2_carry_2, n3_2_1_2_sum, n3_2_1_3_carry_2, n3_2_1_3_sum, n3_2_1_4_sum, not_1_out,
       not_2_out, or_1_out, or_2_out, or_3_out, or_4_out, undriven;

  _3_2_1 u_3_2_1_1 (.Carry(1'b0), .A(1'b1), .B(A0), .Sum(n3_2_1_1_sum), .Carry_2(n3_2_1_1_carry_2));
  _3_2_1 u_3_2_1_2 (.Carry(n3_2_1_1_carry_2), .A(1'b0), .B(A1), .Sum(n3_2_1_2_sum), .Carry_2(n3_2_1_2_carry_2));
  _3_2_1 u_3_2_1_3 (.Carry(n3_2_1_2_carry_2), .A(1'b0), .B(A2), .Sum(n3_2_1_3_sum), .Carry_2(n3_2_1_3_carry_2));
  _3_2_1 u_3_2_1_4 (.Carry(n3_2_1_3_carry_2), .A(A3), .B(1'b0), .Sum(n3_2_1_4_sum));  // open: Carry_2
  Clock clock_1 (.out(clock_1_out));
  not not_1 (not_1_out, R);
  Multiplexer #(.enable("false")) multiplexer_1 (
    .in0(1'b1), .in1(clock_1_out), .out(multiplexer_1_out), .sel(not_2_out));
  not not_2 (not_2_out, S);
  and and_1 (and_1_out, n3_2_1_1_sum, not_1_out);
  and and_2 (and_2_out, n3_2_1_2_sum, not_1_out);
  and and_3 (and_3_out, n3_2_1_3_sum, not_1_out);
  and and_4 (and_4_out, n3_2_1_4_sum, not_1_out);
  or or_1 (or_1_out, R, and_1_out);
  or or_2 (or_2_out, R, and_2_out);
  or or_3 (or_3_out, 1'b0, and_3_out);
  or or_4 (or_4_out, 1'b0, and_4_out);
  D_Flip_Flop d_ff_1 (
    .clk(multiplexer_1_out), .D(or_1_out), .Q(A0), .preset(undriven), .en(undriven));  // open: Qn, reset
  D_Flip_Flop d_ff_2 (.clk(multiplexer_1_out), .D(or_2_out), .Q(A1));  // open: Qn, preset, en, reset
  D_Flip_Flop d_ff_3 (.clk(multiplexer_1_out), .D(or_3_out), .Q(A2));  // open: Qn, preset, en, reset
  D_Flip_Flop d_ff_4 (.clk(multiplexer_1_out), .D(or_4_out), .Q(A3));  // open: Qn, preset, en, reset
endmodule

module _4_2_3 (
  input  S,
  output A0,
  output A1,
  output A2,
  output A3
);

  wire and_1_out, and_2_out, and_3_out, and_4_out, and_5_out, clock_1_out, multiplexer_1_out,
       n3_2_1_1_carry_2, n3_2_1_1_sum, n3_2_1_2_carry_2, n3_2_1_2_sum, n3_2_1_3_carry_2, n3_2_1_3_sum,
       n3_2_1_4_sum, not_1_out, not_2_out, or_1_out, or_2_out, or_3_out, or_4_out, undriven;

  _3_2_1 u_3_2_1_1 (.Carry(1'b0), .A(1'b1), .B(A0), .Sum(n3_2_1_1_sum), .Carry_2(n3_2_1_1_carry_2));
  _3_2_1 u_3_2_1_2 (.Carry(n3_2_1_1_carry_2), .A(1'b0), .B(A1), .Sum(n3_2_1_2_sum), .Carry_2(n3_2_1_2_carry_2));
  _3_2_1 u_3_2_1_3 (.Carry(n3_2_1_2_carry_2), .A(1'b0), .B(A2), .Sum(n3_2_1_3_sum), .Carry_2(n3_2_1_3_carry_2));
  _3_2_1 u_3_2_1_4 (.Carry(n3_2_1_3_carry_2), .A(A3), .B(1'b0), .Sum(n3_2_1_4_sum));  // open: Carry_2
  and and_1 (and_1_out, ~A0, A1, A2, A3);  // AND_Gate
  Clock clock_1 (.out(clock_1_out));
  not not_1 (not_1_out, and_1_out);
  Multiplexer #(.enable("false")) multiplexer_1 (
    .in0(1'b1), .in1(clock_1_out), .out(multiplexer_1_out), .sel(not_2_out));
  not not_2 (not_2_out, S);
  and and_2 (and_2_out, n3_2_1_1_sum, not_1_out);
  and and_3 (and_3_out, n3_2_1_2_sum, not_1_out);
  and and_4 (and_4_out, n3_2_1_3_sum, not_1_out);
  and and_5 (and_5_out, n3_2_1_4_sum, not_1_out);
  or or_1 (or_1_out, and_1_out, and_2_out);
  or or_2 (or_2_out, and_1_out, and_3_out);
  or or_3 (or_3_out, 1'b0, and_4_out);
  or or_4 (or_4_out, 1'b0, and_5_out);
  D_Flip_Flop d_ff_1 (
    .clk(multiplexer_1_out), .D(or_1_out), .Q(A0), .preset(undriven), .en(undriven));  // open: Qn, reset
  D_Flip_Flop d_ff_2 (.clk(multiplexer_1_out), .D(or_2_out), .Q(A1));  // open: Qn, preset, en, reset
  D_Flip_Flop d_ff_3 (.clk(multiplexer_1_out), .D(or_3_out), .Q(A2));  // open: Qn, preset, en, reset
  D_Flip_Flop d_ff_4 (.clk(multiplexer_1_out), .D(or_4_out), .Q(A3));  // open: Qn, preset, en, reset
endmodule
