// Logisim project Es 6.circ as structural Verilog: 5 circuits, main circuit 6.1.1
module _6_1_1 (
  input  in_1,
  output out_2
);

  wire d_ff_1_q, d_ff_1_qn, d_ff_2_qn;

  D_Flip_Flop d_ff_1 (.clk(in_1), .D(d_ff_1_qn), .Q(d_ff_1_q), .Qn(d_ff_1_qn));  // open: preset, en, reset
  D_Flip_Flop d_ff_2 (.clk(d_ff_1_q), .D(d_ff_2_qn), .Q(out_2), .Qn(d_ff_2_qn));  // open: preset, en, reset
endmodule

module _6_1_2 (
  input  CK,
  output out_2,
  output out_3
);

  wire d_ff_1_q;

  D_Flip_Flop d_ff_1 (.clk(CK), .D(out_2), .Q(d_ff_1_q), .Qn(out_2));  // open: preset, en, reset
  D_Flip_Flop d_ff_2 (.clk(d_ff_1_q), .D(out_3), .Qn(out_3));  // open: Q, preset, en, reset
endmodule

module _6_2 (
  input  CK,
  input  in_2,
  input  in_3,
  input  in_4,
  input  in_5,
  output out_6
);

  wire n6_1_2_1_out_2, n6_1_2_1_out_3;

  _6_1_2 u_6_1_2_1 (.CK(CK), .out_2(n6_1_2_1_out_2), .out_3(n6_1_2_1_out_3));
  _2_2_2 u_2_2_2_1 (
    .A(in_2), .B(in_3), .C(in_4), .D(in_5), .Sel1(n6_1_2_1_out_3), .Sel2(n6_1_2_1_out_2), .out_7(out_6));
endmodule

module _6_3 (
  input  CK,
  input  in_2,
  output out_3,
  output out_4,
  output out_5,
  output out_6
);

  wire d_ff_1_q, d_ff_2_q, d_ff_3_q, d_ff_4_q, n6_1_1_1_out_2;

  D_Flip_Flop d_ff_1 (.clk(CK), .D(in_2), .Q(d_ff_1_q));  // open: Qn, preset, en, reset
  D_Flip_Flop d_ff_2 (.clk(CK), .D(d_ff_1_q), .Q(d_ff_2_q));  // open: Qn, preset, en, reset
  D_Flip_Flop d_ff_3 (.clk(CK), .D(d_ff_2_q), .Q(d_ff_3_q));  // open: Qn, preset, en, reset
  _6_1_1 u_6_1_1_1 (.in_1(CK), .out_2(n6_1_1_1_out_2));
  D_Flip_Flop d_ff_4 (.clk(CK), .D(d_ff_3_q), .Q(d_ff_4_q));  // open: Qn, preset, en, reset
  D_Flip_Flop d_ff_5 (.clk(n6_1_1_1_out_2), .D(d_ff_4_q), .Q(out_3));  // open: Qn, preset, en, reset
  D_Flip_Flop d_ff_6 (.clk(n6_1_1_1_out_2), .D(d_ff_3_q), .Q(out_4));  // open: Qn, preset, en, reset
  D_Flip_Flop d_ff_7 (.clk(n6_1_1_1_out_2), .D(d_ff_2_q), .Q(out_5));  // open: Qn, preset, en, reset
  D_Flip_Flop d_ff_8 (.clk(n6_1_1_1_out_2), .D(d_ff_1_q), .Q(out_6));  // open: Qn, preset, en, reset
endmodule

module _6_4 (
  input  in_1,
  input  in_2,
  input  in_3,
  input  in_4,
  output out_5,
  output out_6,
  output out_7,
  output out_8
);

  wire clock_1_out, n6_2_1_out_6;

  Clock clock_1 (.out(clock_1_out));
  _6_2 u_6_2_1 (.CK(clock_1_out), .in_2(in_1), .in_3(in_2), .in_4(in_3), .in_5(in_4), .out_6(n6_2_1_out_6));
  _6_3 u_6_3_1 (.CK(clock_1_out), .in_2(n6_2_1_out_6), .out_3(out_5), .out_4(out_6), .out_5(out_7), .out_6(out_8));
endmodule
