// Logisim project Es 7.circ as structural Verilog: 7 circuits, main circuit 7.1.1
module _7_1_1 (
  input  in_1,
  input  in_2,
  input  in_3,
  input  in_4,
  input  in_5,
  input  in_6,
  input  in_7,
  input  in_8,
  output out_9,
  output out_10,
  output out_11,
  output out_12,
  output OFW
);

  wire not_1_out;

  _3_2_2 u_3_2_2_1 (
    .A0(in_1), .B0(in_5), .A1(in_2), .B1(in_6), .A2(in_3), .B2(in_7), .A3(in_4), .B3(in_8), .C0(out_9),
    .C1(out_10), .C2(out_11), .C3(out_12));  // open: C4__OWF
  not not_1 (not_1_out, out_12);
  and and_1 (OFW, not_1_out, in_8, in_4);
endmodule

module _7_1_2 (
  input  in_1,
  input  in_2,
  input  in_3,
  input  in_4,
  input  in_5,
  input  in_6,
  input  in_7,
  input  in_8,
  output out_9,
  output out_10,
  output out_11,
  output out_12,
  output OFW
);

  wire not_1_out;

  _3_2_2 u_3_2_2_1 (
    .A0(in_1), .B0(in_5), .A1(in_2), .B1(in_6), .A2(in_3), .B2(in_7), .A3(in_4), .B3(in_8), .C0(out_9),
    .C1(out_10), .C2(out_11), .C3(out_12));  // open: C4__OWF
  not not_1 (not_1_out, out_12);
  and and_1 (OFW, not_1_out, in_8, in_4);
endmodule

module _7_1_3 (
  input  in_1,
  input  in_2,
  input  m,
  input  in_4,
  input  in_5,
  input  in_6,
  input  in_7,
  input  in_8,
  output m___n,
  output m____n,
  output m___n_2
);

  wire and_1_out, and_2_out, and_3_out, and_4_out, and_5_out, and_6_out, and_7_out, and_8_out, and_9_out,
       and_10_out, not_1_out, not_2_out, not_3_out, not_4_out, not_5_out, not_6_out, not_7_out, not_8_out,
       not_9_out, not_10_out, or_1_out, xor_1_out, xor_2_out, xor_3_out, xor_4_out;

  not not_1 (not_1_out, in_1);
  not not_2 (not_2_out, in_2);
  not not_3 (not_3_out, m);
  not not_4 (not_4_out, in_8);
  and and_1 (and_1_out, in_5, not_1_out);
  and and_2 (and_2_out, in_6, not_2_out);
  and and_3 (and_3_out, in_7, not_3_out);
  and and_4 (and_4_out, not_4_out, in_4);
  and and_5 (and_5_out, in_4, in_8);
  not not_5 (not_5_out, and_3_out);
  or or_1 (or_1_out, and_4_out, and_5_out);
  and and_6 (and_6_out, and_2_out, not_5_out);
  and and_7 (and_7_out, and_1_out, not_6_out);
  not not_6 (not_6_out, and_6_out);
  xor xor_1 (xor_1_out, in_1, in_5);
  xor xor_2 (xor_2_out, in_2, in_6);
  xor xor_3 (xor_3_out, m, in_7);
  xor xor_4 (xor_4_out, in_4, in_8);
  not not_7 (not_7_out, xor_1_out);
  not not_8 (not_8_out, xor_2_out);
  not not_9 (not_9_out, xor_3_out);
  not not_10 (not_10_out, xor_4_out);
  and and_8 (and_8_out, and_7_out, or_1_out);
  and and_9 (and_9_out, and_6_out, or_1_out);
  and and_10 (and_10_out, and_3_out, or_1_out);
  and and_11 (m___n_2, not_7_out, not_8_out, not_9_out, not_10_out);
  or or_2 (m___n, and_8_out, and_9_out, and_10_out, or_1_out);
  or or_3 (m____n, m___n, m___n_2);

  // Notes on the sheet:
  //   n
endmodule

module _7_2_1 (
  input  T,
  output out_2
);

  wire clock_1_out, d_ff_1_qn, not_1_out, xor_1_out;

  Clock clock_1 (.out(clock_1_out));
  not not_1 (not_1_out, T);
  xor xor_1 (xor_1_out, not_1_out, d_ff_1_qn);
  D_Flip_Flop d_ff_1 (.clk(clock_1_out), .D(xor_1_out), .Q(out_2), .Qn(d_ff_1_qn));  // open: preset, en, reset
endmodule

module _7_2_2 (
  output out_1
);

  wire clock_1_out, d_ff_1_qn;

  Clock clock_1 (.out(clock_1_out));
  D_Flip_Flop d_ff_1 (.clk(clock_1_out), .D(d_ff_1_qn), .Q(out_1), .Qn(d_ff_1_qn));  // open: preset, en, reset
endmodule

module _7_2_3 (
  output out_1
);

  wire clock_1_out, d_ff_1_q, d_ff_1_qn, d_ff_2_qn;

  Clock clock_1 (.out(clock_1_out));
  D_Flip_Flop d_ff_1 (.clk(clock_1_out), .D(d_ff_1_qn), .Q(d_ff_1_q), .Qn(d_ff_1_qn));  // open: preset, en, reset
  D_Flip_Flop d_ff_2 (.clk(d_ff_1_q), .D(d_ff_2_qn), .Q(out_1), .Qn(d_ff_2_qn));  // open: preset, en, reset
endmodule

module _7_2_4 (
  output out_1,
  output out_2
);

  wire clock_1_out, d_ff_1_q;

  Clock clock_1 (.out(clock_1_out));
  D_Flip_Flop d_ff_1 (.clk(clock_1_out), .D(out_1), .Q(d_ff_1_q), .Qn(out_1));  // open: preset, en, reset
  D_Flip_Flop d_ff_2 (.clk(d_ff_1_q), .D(out_2), .Qn(out_2));  // open: Q, preset, en, reset
endmodule
