// Logisim project Es 1.circ as structural Verilog: 3 circuits, main circuit 1.1
module _1_1 (
  input  in_1,
  input  in_2,
  input  in_3,
  input  in_4,
  input  in_5,
  input  in_6,
  output out_7,
  output out_8
);

  wire and_1_out, and_2_out, and_3_out, and_4_out, and_5_out, and_6_out, and_7_out, not_1_out, not_2_out,
       not_3_out, not_4_out, not_5_out, not_6_out;

  not not_1 (not_1_out, in_1);
  not not_2 (not_2_out, in_3);
  not not_3 (not_3_out, in_2);
  and and_1 (and_1_out, not_1_out, not_3_out, not_2_out);
  and and_2 (and_2_out, not_1_out, not_3_out, in_3);
  and and_3 (and_3_out, not_1_out, in_2, not_2_out);
  and and_4 (and_4_out, in_1, not_3_out, not_2_out);
  or or_1 (out_7, and_1_out, and_2_out, and_3_out, and_4_out);
  not not_4 (not_4_out, in_4);
  not not_5 (not_5_out, in_5);
  not not_6 (not_6_out, in_6);
  and and_5 (and_5_out, not_4_out, not_5_out);
  and and_6 (and_6_out, not_4_out, not_6_out);
  and and_7 (and_7_out, not_5_out, not_6_out);
  or or_2 (out_8, and_5_out, and_6_out, and_7_out);

  // Notes on the sheet:
  //   Versione completa
  //   Versione minimizzata
endmodule

module _1_2 (
  input  A,
  input  B,
  input  C,
  input  A_2,
  input  B_2,
  input  C_2,
  output out_7,
  output out_8
);

  wire and_1_out, and_2_out, and_3_out, and_4_out, not_1_out, not_2_out, not_3_out, not_4_out, not_5_out,
       not_6_out, xor_1_out, xor_2_out, xor_3_out, xor_4_out;

  not not_1 (not_1_out, A);
  not not_2 (not_2_out, B);
  not not_3 (not_3_out, C);
  and and_1 (and_1_out, not_1_out, not_2_out, C);
  and and_2 (and_2_out, not_1_out, B, not_3_out);
  and and_3 (and_3_out, A, not_2_out, not_3_out);
  and and_4 (and_4_out, A, B, C);
  or or_1 (out_8, and_1_out, and_2_out, and_3_out, and_4_out);
  not not_4 (not_4_out, A_2);
  not not_5 (not_5_out, B_2);
  not not_6 (not_6_out, C_2);
  ExactlyOne xor_1 (.out(xor_1_out), .in0(A_2), .in1(B_2), .in2(C_2));
  ExactlyOne xor_2 (.out(xor_2_out), .in0(A_2), .in1(not_5_out), .in2(not_6_out));
  ExactlyOne xor_3 (.out(xor_3_out), .in0(not_4_out), .in1(B_2), .in2(not_6_out));
  ExactlyOne xor_4 (.out(xor_4_out), .in0(not_4_out), .in1(not_5_out), .in2(C_2));
  or or_2 (out_7, xor_1_out, xor_2_out, xor_3_out, xor_4_out);

  // Notes on the sheet:
  //   Versione semplice
  //   Versione xor
endmodule

module Versione_duale (
  input  A1,
  input  A2,
  input  B1,
  input  B2,
  input  A1_2,
  input  A2_2,
  input  B1_2,
  input  B2_2,
  output out_9,
  output out_10
);

  wire and_1_out, and_2_out, and_3_out, and_4_out, and_5_out, and_6_out, not_1_out, not_2_out, not_3_out,
       not_4_out, not_6_out, not_7_out, not_8_out, not_9_out, or_1_out, or_2_out, or_3_out, or_4_out,
       or_5_out, or_6_out, or_7_out, or_8_out, or_9_out;

  not not_1 (not_1_out, A1);
  not not_2 (not_2_out, A2);
  not not_3 (not_3_out, B1);
  not not_4 (not_4_out, B2);
  and and_1 (and_1_out, not_1_out, A2, not_3_out, not_4_out);
  and and_2 (and_2_out, A1, not_2_out, not_3_out, not_4_out);
  and and_3 (and_3_out, A1, not_2_out, not_3_out, B2);
  and and_4 (and_4_out, A1, A2, not_3_out, not_4_out);
  and and_5 (and_5_out, A1, A2, not_3_out, B2);
  and and_6 (and_6_out, A1, A2, B1, not_4_out);
  or or_1 (or_1_out, and_1_out, and_2_out, and_3_out);
  or or_2 (or_2_out, and_4_out, and_5_out, and_6_out);
  or or_3 (or_3_out, or_1_out, or_2_out);
  not not_5 (out_9, or_3_out);
  not not_6 (not_6_out, A1_2);
  not not_7 (not_7_out, A2_2);
  not not_8 (not_8_out, B1_2);
  not not_9 (not_9_out, B2_2);
  or or_4 (or_4_out, A1_2, not_7_out, B1_2, B2_2);
  or or_5 (or_5_out, not_6_out, A2_2, B1_2, B2_2);
  or or_6 (or_6_out, not_6_out, A2_2, B1_2, not_9_out);
  or or_7 (or_7_out, not_6_out, not_7_out, B1_2, B2_2);
  or or_8 (or_8_out, not_6_out, not_7_out, B1_2, not_9_out);
  or or_9 (or_9_out, not_6_out, not_7_out, not_8_out, B2_2);
  and and_7 (out_10, or_4_out, or_5_out, or_6_out, or_7_out, or_8_out, or_9_out);

  // Notes on the sheet:
  //   Versione semplice
  //   Versione duale
endmodule
