// Logisim project Es 2.circ as structural Verilog: 6 circuits, main circuit 2.1.1
module _2_1_1 (
  input  in_1,
  input  in_2,
  input  in_3,
  input  in_4,
  output out_5
);

  wire and_1_out, and_2_out, and_3_out, and_4_out, and_5_out, and_6_out, and_7_out, not_1_out, not_2_out,
       not_3_out, not_4_out;

  not not_1 (not_1_out, in_1);
  not not_2 (not_2_out, in_2);
  not not_3 (not_3_out, in_3);
  not not_4 (not_4_out, in_4);
  and and_1 (and_1_out, not_1_out, not_2_out, not_3_out, in_4);
  and and_2 (and_2_out, not_1_out, not_2_out, in_3, not_4_out);
  and and_3 (and_3_out, not_1_out, not_2_out, in_3, in_4);
  and and_4 (and_4_out, not_1_out, in_2, not_3_out, not_4_out);
  and and_5 (and_5_out, not_1_out, in_2, in_3, in_4);
  and and_6 (and_6_out, in_1, not_2_out, in_3, in_4);
  and and_7 (and_7_out, in_1, in_2, not_3_out, in_4);
  or or_1 (out_5, and_1_out, and_2_out, and_3_out, and_4_out, and_5_out, and_6_out, and_7_out);
endmodule

module _2_1_2 (
  input  in_1,
  input  in_2,
  input  in_3,
  input  in_4,
  output out_5
);

  wire and_1_out, and_2_out, not_1_out, not_2_out, not_3_out, not_4_out;

  not not_1 (not_1_out, in_1);
  not not_2 (not_2_out, in_2);
  not not_3 (not_3_out, in_3);
  not not_4 (not_4_out, in_4);
  and and_1 (and_1_out, not_1_out, in_2, in_3, not_4_out);
  and and_2 (and_2_out, not_1_out, in_2, not_3_out, in_4);
  or or_1 (out_5, and_1_out, and_2_out, not_4_out);
endmodule

module _2_2_1 (
  input  A,
  input  B,
  input  Sel,
  output out_4
);

  wire and_1_out, and_2_out;

  and and_1 (and_1_out, A, ~Sel);  // AND_Gate
  and and_2 (and_2_out, B, Sel);
  or or_1 (out_4, and_1_out, and_2_out);
endmodule

module _2_2_2 (
  input  A,
  input  B,
  input  C,
  input  D,
  input  Sel1,
  input  Sel2,
  output out_7
);

  wire and_1_out, and_2_out, and_3_out, n2_2_1_1_out_4, n2_2_1_2_out_4;

  _2_2_1 u_2_2_1_1 (.A(A), .B(B), .Sel(and_1_out), .out_4(n2_2_1_1_out_4));
  and and_1 (and_1_out, ~Sel1, Sel2);  // AND_Gate
  _2_2_1 u_2_2_1_2 (.A(n2_2_1_1_out_4), .B(C), .Sel(and_2_out), .out_4(n2_2_1_2_out_4));
  and and_2 (and_2_out, Sel1, ~Sel2);  // AND_Gate
  _2_2_1 u_2_2_1_3 (.A(n2_2_1_2_out_4), .B(D), .Sel(and_3_out), .out_4(out_7));
  and and_3 (and_3_out, ~and_1_out, Sel2);  // AND_Gate
endmodule

module _2_3_1 (
  input  A,
  input  B,
  input  Enable,
  output out_4,
  output out_5,
  output out_6,
  output out_7
);

  wire and_1_out, and_2_out, and_3_out, and_4_out, not_1_out, not_2_out, not_3_out, not_4_out;

  not not_1 (not_1_out, A);
  not not_2 (not_2_out, B);
  not not_3 (not_3_out, A);
  not not_4 (not_4_out, B);
  and and_1 (and_1_out, not_1_out, not_2_out);
  and and_2 (and_2_out, not_3_out, B);
  and and_3 (and_3_out, A, not_4_out);
  and and_4 (and_4_out, A, B);
  and and_5 (out_4, and_1_out, Enable);
  and and_6 (out_5, and_2_out, Enable);
  and and_7 (out_6, and_3_out, Enable);
  and and_8 (out_7, and_4_out, Enable);
endmodule

module _2_3_2 (
  input  in_1,
  input  in_2,
  input  in_3,
  input  Enable,
  input  in_5,
  input  in_6,
  input  in_7,
  input  in_8,
  input  Enable_2,
  output out_10,
  output out_11,
  output out_12,
  output out_13,
  output out_14,
  output out_15,
  output out_16,
  output out_17,
  output out_18,
  output out_19,
  output out_20,
  output out_21,
  output out_22,
  output out_23,
  output out_24,
  output out_25,
  output out_26,
  output out_27,
  output out_28,
  output out_29,
  output out_30,
  output out_31,
  output out_32,
  output out_33
);

  wire and_1_out, and_2_out, and_3_out, and_4_out, and_5_out, and_6_out, and_7_out, and_8_out, and_9_out,
       and_10_out, and_11_out, and_12_out, and_13_out, and_14_out, and_15_out, and_16_out, and_17_out,
       and_18_out, and_19_out, and_20_out, and_21_out, and_22_out, and_23_out, and_24_out, n2_3_1_1_out_4,
       n2_3_1_1_out_5, n2_3_1_1_out_6, n2_3_1_1_out_7, n2_3_1_2_out_4, n2_3_1_2_out_5, n2_3_1_2_out_6,
       n2_3_1_2_out_7, n2_3_1_3_out_4, n2_3_1_3_out_5, n2_3_1_3_out_6, n2_3_1_3_out_7, not_1_out;

  _2_3_1 u_2_3_1_1 (
    .A(in_2), .B(in_3), .Enable(Enable), .out_4(n2_3_1_1_out_4), .out_5(n2_3_1_1_out_5),
    .out_6(n2_3_1_1_out_6), .out_7(n2_3_1_1_out_7));
  _2_3_1 u_2_3_1_2 (
    .A(in_5), .B(in_6), .Enable(Enable_2), .out_4(n2_3_1_2_out_4), .out_5(n2_3_1_2_out_5),
    .out_6(n2_3_1_2_out_6), .out_7(n2_3_1_2_out_7));
  _2_3_1 u_2_3_1_3 (
    .A(in_7), .B(in_8), .Enable(Enable_2), .out_4(n2_3_1_3_out_4), .out_5(n2_3_1_3_out_5),
    .out_6(n2_3_1_3_out_6), .out_7(n2_3_1_3_out_7));
  not not_1 (not_1_out, in_1);
  and and_1 (and_1_out, n2_3_1_1_out_4, not_1_out);
  and and_2 (and_2_out, n2_3_1_1_out_5, not_1_out);
  and and_3 (and_3_out, n2_3_1_1_out_6, not_1_out);
  and and_4 (and_4_out, n2_3_1_1_out_7, not_1_out);
  and and_5 (and_5_out, n2_3_1_1_out_4, in_1);
  and and_6 (and_6_out, n2_3_1_1_out_5, in_1);
  and and_7 (and_7_out, n2_3_1_1_out_6, in_1);
  and and_8 (and_8_out, n2_3_1_1_out_7, in_1);
  and and_9 (and_9_out, n2_3_1_2_out_4, n2_3_1_3_out_4);
  and and_10 (and_10_out, n2_3_1_2_out_4, n2_3_1_3_out_5);
  and and_11 (and_11_out, n2_3_1_2_out_4, n2_3_1_3_out_6);
  and and_12 (and_12_out, n2_3_1_2_out_4, n2_3_1_3_out_7);
  and and_13 (and_13_out, n2_3_1_2_out_5, n2_3_1_3_out_4);
  and and_14 (and_14_out, n2_3_1_2_out_5, n2_3_1_3_out_5);
  and and_15 (and_15_out, n2_3_1_2_out_5, n2_3_1_3_out_6);
  and and_16 (and_16_out, n2_3_1_2_out_5, n2_3_1_3_out_7);
  and and_17 (and_17_out, n2_3_1_2_out_6, n2_3_1_3_out_4);
  and and_18 (and_18_out, n2_3_1_2_out_6, n2_3_1_3_out_5);
  and and_19 (and_19_out, n2_3_1_2_out_6, n2_3_1_3_out_6);
  and and_20 (and_20_out, n2_3_1_2_out_6, n2_3_1_3_out_7);
  and and_21 (and_21_out, n2_3_1_2_out_7, n2_3_1_3_out_4);
  and and_22 (and_22_out, n2_3_1_2_out_7, n2_3_1_3_out_5);
  and and_23 (and_23_out, n2_3_1_2_out_7, n2_3_1_3_out_6);
  and and_24 (and_24_out, n2_3_1_2_out_7, n2_3_1_3_out_7);
  and and_25 (out_10, and_1_out, Enable);
  and and_26 (out_11, and_2_out, Enable);
  and and_27 (out_12, and_3_out, Enable);
  and and_28 (out_13, and_4_out, Enable);
  and and_29 (out_14, and_5_out, Enable);
  and and_30 (out_15, and_6_out, Enable);
  and and_31 (out_16, and_7_out, Enable);
  and and_32 (out_17, and_8_out, Enable);
  and and_33 (out_18, and_9_out, Enable_2);
  and and_34 (out_19, and_10_out, Enable_2);
  and and_35 (out_20, and_11_out, Enable_2);
  and and_36 (out_21, and_12_out, Enable_2);
  and and_37 (out_22, and_13_out, Enable_2);
  and and_38 (out_23, and_14_out, Enable_2);
  and and_39 (out_24, and_15_out, Enable_2);
  and and_40 (out_25, and_16_out, Enable_2);
  and and_41 (out_26, and_17_out, Enable_2);
  and and_42 (out_27, and_18_out, Enable_2);
  and and_43 (out_28, and_19_out, Enable_2);
  and and_44 (out_29, and_20_out, Enable_2);
  and and_45 (out_30, and_21_out, Enable_2);
  and and_46 (out_31, and_22_out, Enable_2);
  and and_47 (out_32, and_23_out, Enable_2);
  and and_48 (out_33, and_24_out, Enable_2);
endmodule
