// Logisim project Es 3.circ as structural Verilog: 4 circuits, main circuit 3.1.1
module _3_1_1 (
  input  A,
  input  B,
  output Sum,
  output Carry
);

  xor xor_1 (Sum, A, B);
  and and_1 (Carry, A, B);
endmodule

module _3_1_2 (
  input  in_1,
  input  in_2,
  input  in_3,
  input  in_4,
  output out_5,
  output out_6,
  output out_7,
  output out_8,
  output out_9
);

  wire n3_1_1_1_carry, n3_1_1_2_carry, n3_1_1_3_carry;

  _3_1_1 u_3_1_1_1 (.A(1'b1), .B(in_1), .Sum(out_5), .Carry(n3_1_1_1_carry));
  _3_1_1 u_3_1_1_2 (.A(n3_1_1_1_carry), .B(in_2), .Sum(out_6), .Carry(n3_1_1_2_carry));
  _3_1_1 u_3_1_1_3 (.A(n3_1_1_2_carry), .B(in_3), .Sum(out_7), .Carry(n3_1_1_3_carry));
  _3_1_1 u_3_1_1_4 (.A(n3_1_1_3_carry), .B(in_4), .Sum(out_8), .Carry(out_9));
endmodule

module _3_2_1 (
  input  Carry,
  input  A,
  input  B,
  output Sum,
  output Carry_2
);

  wire n3_1_1_1_carry, n3_1_1_1_sum, n3_1_1_2_carry;

  _3_1_1 u_3_1_1_1 (.A(A), .B(B), .Sum(n3_1_1_1_sum), .Carry(n3_1_1_1_carry));
  _3_1_1 u_3_1_1_2 (.A(Carry), .B(n3_1_1_1_sum), .Sum(Sum), .Carry(n3_1_1_2_carry));
  or or_1 (Carry_2, n3_1_1_2_carry, n3_1_1_1_carry);
endmodule

module _3_2_2 (
  input  A0,
  input  B0,
  input  A1,
  input  B1,
  input  A2,
  input  B2,
  input  A3,
  input  B3,
  output C0,
  output C1,
  output C2,
  output C3,
  output C4__OWF
);

  wire n3_2_1_1_carry_2, n3_2_1_2_carry_2, n3_2_1_3_carry_2;

  _3_2_1 u_3_2_1_1 (.Carry(1'b0), .A(A0), .B(B0), .Sum(C0), .Carry_2(n3_2_1_1_carry_2));
  _3_2_1 u_3_2_1_2 (.Carry(n3_2_1_1_carry_2), .A(A1), .B(B1), .Sum(C1), .Carry_2(n3_2_1_2_carry_2));
  _3_2_1 u_3_2_1_3 (.Carry(n3_2_1_2_carry_2), .A(A2), .B(B2), .Sum(C2), .Carry_2(n3_2_1_3_carry_2));
  _3_2_1 u_3_2_1_4 (.Carry(n3_2_1_3_carry_2), .A(A3), .B(B3), .Sum(C3), .Carry_2(C4__OWF));
endmodule
