// Logisim project Es 5.circ as structural Verilog: 5 circuits, main circuit 5.1.1
module _5_1_1 (
  input  Clock,
  input  Input,
  output out_3
);

  wire and_1_out, and_2_out, and_3_out, and_4_out, and_5_out, and_6_out, d_ff_1_q, d_ff_2_q, d_ff_3_q,
       or_1_out, or_2_out;

  Clock clock_1 ();  // open: out
  and and_1 (and_1_out, ~d_ff_1_q, d_ff_2_q, d_ff_3_q, Input);  // AND_Gate
  and and_2 (and_2_out, ~d_ff_1_q, d_ff_2_q, ~d_ff_3_q, Input);  // AND_Gate
  and and_3 (and_3_out, d_ff_1_q, ~d_ff_2_q, ~d_ff_3_q, ~Input);  // AND_Gate
  or or_1 (or_1_out, and_2_out, and_3_out, and_4_out);
  and and_4 (and_4_out, ~d_ff_1_q, d_ff_3_q, ~Input);  // AND_Gate
  and and_5 (and_5_out, ~d_ff_1_q, ~d_ff_2_q, Input);  // AND_Gate
  and and_6 (and_6_out, ~d_ff_3_q, Input);  // AND_Gate
  or or_2 (or_2_out, and_5_out, and_6_out);
  and and_7 (out_3, Input, d_ff_1_q, ~d_ff_2_q, ~d_ff_3_q);  // AND_Gate
  D_Flip_Flop d_ff_1 (.clk(Clock), .D(and_1_out), .Q(d_ff_1_q));  // open: Qn, preset, en, reset
  D_Flip_Flop d_ff_2 (.clk(Clock), .D(or_1_out), .Q(d_ff_2_q));  // open: Qn, preset, en, reset
  D_Flip_Flop d_ff_3 (.clk(Clock), .D(or_2_out), .Q(d_ff_3_q));  // open: Qn, preset, en, reset

  // Notes on the sheet:
  //   S1
  //   S2
  //   S3
endmodule

module _5_1_2 (
  input  Clock,
  input  Input,
  output out_3
);

  wire d_ff_1_q, d_ff_2_q, d_ff_3_q, d_ff_4_q, not_1_out;

  D_Flip_Flop d_ff_1 (.clk(Clock), .D(Input), .Q(d_ff_1_q));  // open: Qn, preset, en, reset
  D_Flip_Flop d_ff_2 (.clk(Clock), .D(d_ff_1_q), .Q(d_ff_2_q));  // open: Qn, preset, en, reset
  D_Flip_Flop d_ff_3 (.clk(Clock), .D(d_ff_2_q), .Q(d_ff_3_q));  // open: Qn, preset, en, reset
  not not_1 (not_1_out, d_ff_3_q);
  D_Flip_Flop d_ff_4 (.clk(Clock), .D(d_ff_3_q), .Q(d_ff_4_q));  // open: Qn, preset, en, reset
  and and_1 (out_3, d_ff_4_q, not_1_out, d_ff_2_q, d_ff_1_q);
endmodule

module _5_1_3 (
  input  in_1,
  output out_2
);

  wire clock_1_out, n5_1_1_1_out_3, n5_1_2_1_out_3;

  Clock clock_1 (.out(clock_1_out));
  _5_1_1 u_5_1_1_1 (.Clock(clock_1_out), .Input(in_1), .out_3(n5_1_1_1_out_3));
  _5_1_2 u_5_1_2_1 (.Clock(clock_1_out), .Input(in_1), .out_3(n5_1_2_1_out_3));
  xnor xnor_1 (out_2, n5_1_1_1_out_3, n5_1_2_1_out_3);
endmodule

module _5_2_1 (
  input  EN,
  input  UP,
  output out_3,
  output out_4,
  output out_5,
  output out_6
);

  wire and_1_out, and_2_out, and_3_out, and_4_out, clock_1_out, multiplexer_1_out, multiplexer_2_out,
       multiplexer_3_out, multiplexer_4_out, n3_2_2_1_c0, n3_2_2_1_c1, n3_2_2_1_c2, n3_2_2_1_c3,
       n3_2_2_1_c4__owf, not_1_out;

  not not_1 (not_1_out, UP);
  Multiplexer multiplexer_1 (.in0(1'b0), .in1(1'b1), .out(multiplexer_1_out), .sel(not_1_out));  // open: en
  Multiplexer multiplexer_2 (.in0(1'b0), .in1(1'b1), .out(multiplexer_2_out), .sel(not_1_out));  // open: en
  Multiplexer multiplexer_3 (.in0(1'b0), .in1(1'b1), .out(multiplexer_3_out), .sel(not_1_out));  // open: en
  Multiplexer multiplexer_4 (.in0(1'b1), .in1(1'b1), .out(multiplexer_4_out), .sel(not_1_out));  // open: en
  and and_1 (and_1_out, multiplexer_1_out, EN);
  and and_2 (and_2_out, multiplexer_2_out, EN);
  and and_3 (and_3_out, multiplexer_3_out, EN);
  and and_4 (and_4_out, multiplexer_4_out, EN);
  _3_2_2 u_3_2_2_1 (
    .A0(out_3), .B0(and_4_out), .A1(out_4), .B1(and_3_out), .A2(out_5), .B2(and_2_out), .A3(out_6),
    .B3(and_1_out), .C0(n3_2_2_1_c0), .C1(n3_2_2_1_c1), .C2(n3_2_2_1_c2), .C3(n3_2_2_1_c3),
    .C4__OWF(n3_2_2_1_c4__owf));
  Clock clock_1 (.out(clock_1_out));
  D_Flip_Flop d_ff_1 (.clk(clock_1_out), .D(n3_2_2_1_c0), .Q(out_3));  // open: Qn, preset, en, reset
  D_Flip_Flop d_ff_2 (.clk(clock_1_out), .D(n3_2_2_1_c1), .Q(out_4));  // open: Qn, preset, en, reset
  D_Flip_Flop d_ff_3 (.clk(clock_1_out), .D(n3_2_2_1_c2), .Q(out_5));  // open: Qn, preset, en, reset
  D_Flip_Flop d_ff_4 (.clk(clock_1_out), .D(n3_2_2_1_c3), .Q(out_6));  // open: Qn, preset, en, reset
endmodule

module _5_3 (
  input  in_1,
  output out_2
);

  wire and_1_out, and_2_out, clock_1_out, d_ff_1_q, d_ff_2_q, d_ff_3_q, d_ff_4_q, d_ff_5_q, n3_2_1_1_carry_2,
       n3_2_1_1_sum, n3_2_1_2_carry_2, n3_2_1_2_sum, not_1_out;

  Clock clock_1 (.out(clock_1_out));
  _3_2_1 u_3_2_1_1 (.Carry(1'b0), .A(1'b1), .B(d_ff_1_q), .Sum(n3_2_1_1_sum), .Carry_2(n3_2_1_1_carry_2));
  _3_2_1 u_3_2_1_2 (.Carry(n3_2_1_1_carry_2), .A(1'b0), .B(d_ff_2_q), .Sum(n3_2_1_2_sum), .Carry_2(n3_2_1_2_carry_2));
  D_Flip_Flop d_ff_1 (.clk(clock_1_out), .D(n3_2_1_1_sum), .Q(d_ff_1_q));  // open: Qn, preset, en, reset
  D_Flip_Flop d_ff_2 (.clk(clock_1_out), .D(n3_2_1_2_sum), .Q(d_ff_2_q));  // open: Qn, preset, en, reset
  D_Flip_Flop d_ff_3 (.clk(clock_1_out), .D(in_1), .Q(d_ff_3_q));  // open: Qn, preset, en, reset
  D_Flip_Flop d_ff_4 (.clk(clock_1_out), .D(d_ff_3_q), .Q(d_ff_4_q));  // open: Qn, preset, en, reset
  and and_1 (and_1_out, d_ff_1_q, d_ff_2_q);
  D_Flip_Flop d_ff_5 (.clk(clock_1_out), .D(d_ff_4_q), .Q(d_ff_5_q));  // open: Qn, preset, en, reset
  not not_1 (not_1_out, d_ff_3_q);
  and and_2 (and_2_out, d_ff_5_q, d_ff_4_q, not_1_out);
  and and_3 (out_2, and_2_out, and_1_out);
endmodule
